# Fritzing sketch din-midi-in-out (saved by Fritzing 0.9.4)
breadboards: 1

parts:
  R1 = Resistor [tolerance=±5% resistance=4.7k package="0603 [SMD]"]
  IC2 = 6n137 Optocoupler [package="DIP (Dual Inline) [THT]"]
  R4 = Resistor [tolerance=±5% resistance=220 package="0603 [SMD]"]
  D2 = Schottky Diode [part_number=1N5817 package="300 mil [THT]"]
  R5 = Resistor [tolerance=±5% resistance=220 package="0603 [SMD]"]
  DIN2 = DIN-5 jack (MIDI) [package=THT]
  Bauteil4 = Arduino Uno (Rev3) - ICSP
  DIN3 = DIN-5 jack (MIDI) [package=THT]
  R6 = Resistor [tolerance=±5% resistance=220 package="0402 [SMD]"]

nets:
  N1: R1.Pin_0, IC2.Ve
  GND: R1.Pin_1, IC2.GND, Bauteil4.GND, DIN3.2
  N2: IC2.Vf+, R4.Pin_1, D2.cathode
  N3: IC2.Vf-, D2.anode, DIN2.4
  N4: IC2.Vo, R5.Pin_1, Bauteil4.D0/RX
  N5: R4.Pin_0, DIN2.5
  N6: R5.Pin_0, Bauteil4.5V, R6.Pin_0
  N7: Bauteil4.D1/TX, DIN3.5
  N8: DIN3.4, R6.Pin_1

notes:
  Opto-isolator Circuit
  Fairchild 6n137 fast opto-coupler, 10Mbits/s rated
  Reverse protection diode is shottky with 30V or higher rating (1N5818 is 30V peak, 1A part)
  Input capacitor C1 should be 30V rated or higher
  Input LED forward voltage ~1.4V typ at 10mA forward current
  1MHz noise cutoff using input RC Low Pass filter, with 0.4us rise time
  Input current limit resistor is two 0.25W 3.3k resistors in parallel
  1.65k delivers
  ~9mA from 15V,
  ~15mA max at rated input voltage
  ~3.7mA at low input of 7V
  max power 300mW in input resistors at max voltage
  Larger input resistor can be used at expense of raising low end input voltage limit for reliable operation
  High level output current max 20uA results in 20mV offset
  Input threshold approx 2.5mA with 1k load resistor
  Designed for inputs of between 7V and 24V, 12-15V nominal
  Ve is for strobing the output and can be left NC if not used as has internal pullup
  Output resistor allows for full output low voltage at >5mA output current
  0.1uF Vcc decoupling required close to Vcc and GND pins
  For connection to Raspberry Pi use a level converter to convert from 5V logic to 3.3V.
  Input 7V to 24V, 15V nominal, 500kHz
  Note that grounds are not joined between source and circuit.
  Example use:
  DCC decoder front end isolator feeding Arduino
  This work by hobbyistdave is licensed under a Creative Commons Attribution-ShareAlike 4.0 International License
  No warranty either express or implied is given.
  This schematic was created with Fritzing.
  Inspired by Geoff Bunza at
  http://model-railroad-hobbyist.com/node/19446
  220 Ω
  4.7kΩ
  DIN MIDI IN
  1N914
  6N138
  DIN MIDI OUT

custom parts:
  6n137 Optocoupler: 6n137 fast Optocoupler. With 8 pins on a 300mil dual inline package (DIP) footprint. Ve is strobe input. Output is inverting.
